// Logisim project ahead.circ as structural Verilog: 2 circuits, main circuit main
module main (
  input  G0,
  input  P0,
  input  C0,
  input  G1,
  input  P1,
  input  G2,
  input  P2,
  input  G3,
  input  P3,
  output c1,
  output c2,
  output c3,
  output c4
);

  wire and_1_out, and_2_out, and_3_out, and_4_out, and_5_out, and_6_out, and_7_out, and_8_out, and_9_out,
       and_10_out;

  and and_1 (and_1_out, P0, C0);
  and and_2 (and_2_out, G0, P1);
  and and_3 (and_3_out, C0, P0, P1);
  or or_1 (c1, G0, and_1_out);
  and and_4 (and_4_out, and_3_out, P2);
  and and_5 (and_5_out, and_2_out, P2);
  and and_6 (and_6_out, P2, G1);
  and and_7 (and_7_out, and_4_out, P3);
  and and_8 (and_8_out, and_5_out, P3);
  and and_9 (and_9_out, and_6_out, P3);
  and and_10 (and_10_out, G2, P3);
  or or_2 (c2, and_2_out, G1, and_3_out);
  or or_3 (c3, and_4_out, G2, and_6_out, and_5_out);
  or or_4 (c4, and_7_out, and_8_out, and_10_out, and_9_out, G3);
endmodule

module lookahead (
  input  in_1,
  input  [3:0] x,
  input  [3:0] y,
  output out_4,
  output out_5,
  output out_6,
  output out_7,
  output out_8
);

  wire and_1_out, and_2_out, and_3_out, and_4_out, main_1_c1, main_1_c2, main_1_c3, xor_1_out, xor_2_out,
       xor_3_out, xor_4_out;

  xor xor_1 (xor_1_out, x[0], y[0]);
  and and_1 (and_1_out, x[0], y[0]);
  xor xor_2 (xor_2_out, x[1], y[1]);
  and and_2 (and_2_out, x[1], y[1]);
  xor xor_3 (xor_3_out, x[2], y[2]);
  and and_3 (and_3_out, x[2], y[2]);
  xor xor_4 (xor_4_out, x[3], y[3]);
  and and_4 (and_4_out, x[3], y[3]);
  main main_1 (
    .G0(and_1_out), .P0(xor_1_out), .C0(in_1), .G1(and_2_out), .P1(xor_2_out), .G2(and_3_out),
    .P2(xor_3_out), .G3(and_4_out), .P3(xor_4_out), .c1(main_1_c1), .c2(main_1_c2), .c3(main_1_c3), .c4(out_4));
  xor xor_5 (out_5, xor_4_out, main_1_c3);
  xor xor_6 (out_6, xor_3_out, main_1_c2);
  xor xor_7 (out_7, xor_2_out, main_1_c1);
  xor xor_8 (out_8, xor_1_out, in_1);
endmodule
